# Fritzing sketch Untitled Sketch (saved by Fritzing 0.9.8b)
circuit board: 16.7197cm x 10.7613cm

parts:
  Part1 = Lithium Ion Polymer Battery 3.7v 500mAh [part_number=1578]  # not connected
  Powerboost_1000C = PowerBoost 1000 Basic
  Raspberry_Pi_4B = Raspberry Pi 4B
  PWM_Servo_Driver = 16-Channel 12-bit PWM Servo Driver - I2C [part_number=1]
  J1 = Basic Servo
  J2 = Basic Servo
  SERVOMOTORS = Basic Servo
  Button = Round Pushbutton
  USB_Battery = 4xAA Switchable Battery Pack w/JST connector  # not connected
  M1 = 7in-display [package=THT]  # not connected

nets:
  GND: Powerboost_1000C.GND, Raspberry_Pi_4B.GND, PWM_Servo_Driver.GND, J1.gnd, J2.gnd, SERVOMOTORS.gnd
  N1: Powerboost_1000C.5.0V, PWM_Servo_Driver.PWRIN
  3V3: Raspberry_Pi_4B.3V3, PWM_Servo_Driver.VCC, Button.leg1
  N2: Raspberry_Pi_4B.GPIO2, PWM_Servo_Driver.SDA
  N3: Raspberry_Pi_4B.GPIO3, PWM_Servo_Driver.SCL
  N4: Raspberry_Pi_4B.GPIO4, PWM_Servo_Driver.OE
  N5: Raspberry_Pi_4B.GPIO24, Button.leg0
  VCC: PWM_Servo_Driver.5.0V, J1.vcc, J2.vcc, SERVOMOTORS.vcc
  N6: PWM_Servo_Driver.PWM2, SERVOMOTORS.pulse
  N7: PWM_Servo_Driver.PWM1, J2.pulse
  N8: PWM_Servo_Driver.PWM0, J1.pulse

custom parts:
  Lithium Ion Polymer Battery 3.7v 500mAh: Lithium ion polymer (also known as 'lipo' or 'lipoly') batteries are thin, light and powerful. The output ranges from 4.2V when completely charged to 3.7V. This battery has a capacity of 500mAh for a total of about 1.9 Wh. The batteries come pre-attached with a genuine 2-pin JST-PH connector as shown and include the necessary protection circuitry.
  PowerBoost 1000 Basic: The PowerBoost 1000 is a little DC/DC boost converter module that can run from 1.8V batteries or higher, and convert the battery output to 5.2V DC for running your 5V projects. At its heart is a TPS61030 boost converter from TI. This boost converter chip has some really nice extras such as low battery detection, 4A internal switch, synchronous conversion, excellent efficiency, and 700KHz high-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
  16-Channel 12-bit PWM Servo Driver - I2C: You want to make a cool robot, maybe a hexapod walker, or maybe just a piece of art with a lot of moving parts. Or maybe you want to drive a lot of LEDs with precise PWM output. Using only two pins, control 16 free-running PWM outputs! You can even chain up 62 breakouts to control up to 992 PWM outputs.
  4xAA Switchable Battery Pack w/JST connector: 4xAA Switchable Battery Pack with JST connector
  7in-display: 7In tft rgb touch screen display.
